# Fritzing sketch overall_schematic (saved by Fritzing 0.6.3b)
breadboards: 1

parts:
  SC1 = SC8560
  U1 = Optocoupler [package=THT]
  U2 = Optocoupler [package=THT]
  Arduino1 = Arduino
  R1 = Resistor [tolerance=±5% resistance=1k package=THT]
  Q1 = NPN-Transistor [package="TO92 [THT]"]
  R2 = Resistor [tolerance=±5% resistance=10k package=THT]

nets:
  N1: SC1.connector14, U1.Pin_1, U2.Pin_5
  N2: SC1.connector17, U2.Pin_4
  N3: SC1.connector19, Q1.C
  N4: SC1.connector28, R2.Pin_0
  N5: U1.Pin_2, R1.Pin_0
  N6: U1.Pin_4, U2.Pin_2, Arduino1.GND
  N7: U1.Pin_5, Arduino1.D5
  N8: U2.Pin_1, Arduino1.D3
  N9: R1.Pin_1, Q1.E
  N10: Q1.B, R2.Pin_1
